# Fritzing sketch drone control schematic (saved by Fritzing 0.8.7b)

parts:
  GY1 = MPU-6050 Board GY-521 [form="♀ (female)" package=THT]
  Part1 = Arduino Uno (Rev3) - ICSP
  U1 = 2.4GHz ANT IC [package=mlp-24]
  M1 = DC Motor  # not connected
  M2 = DC Motor  # not connected
  M3 = DC Motor  # not connected
  M4 = DC Motor  # not connected
  U2 = LIPO-2000mAh [package=lipo-2000]
  Eleman1 = LilyPad Slide Switch
  D1 = Diode [package=diode-1n4001]
  R1 = Resistor [package="2010 [SMD]"]
  R2 = Resistor [package="2010 [SMD]"]  # not connected

nets:
  N1: GY1.pin1, Part1.5V
  N2: GY1.pin2, Part1.GND
  N3: GY1.pin3, Part1.A5/SCL
  N4: GY1.pin4, Part1.A4/SDA
  N5: Part1.A0, R1.Pin_0
  N6: Part1.D8, U1.BR2
  N7: Part1.D9_PWM, U1.BR1
  N8: Part1.D10_PWM/SS, U1.EXT32K
  N9: Part1.D11_PWM/MOSI, U1.RXD
  N10: U2.+, Eleman1.ON
  N11: U2.-, Eleman1.OFF
  N12: D1.A, R1.Pin_1

notes:
  2.4 Ghz Receiver
  ESC 1
  Right front
  ccw
  ESC 2
  Right rear
  cw
  ESC 3
  Left rear
  ccw
  ESC 4
  Left front
  cw
  Assume its battery controller
  lipo 3cell and 11.1V battery
  use brushless engine and 3 cable for each of it will be connnected to the ESC

custom parts:
  MPU-6050 Board GY-521: Acelerometro y Giroscopio MPU-6050 Board GY-521
